# Fritzing sketch neopixel_truck_lights (saved by Fritzing 0.9.2b)
breadboards: 1

parts:
  NEOPIXEL1 = Neopixel Strip -- Black (60/m)
  TRINKET1 = Trinket 5V
  C1 = Electrolytic Capacitor [capacitance=0.47mF voltage=10V package="300 mil [THT, electrolytic]"]
  R1 = Resistor [tolerance=±5% resistance=330 package=THT]
  R2 = Resistor [tolerance=±5% resistance=470 package=THT]
  S1 = Momentary Switch [package=ksa_sealed_tac_switch]

nets:
  N1: NEOPIXEL1.+5V, TRINKET1.no_name_yet#10, C1.+
  N2: NEOPIXEL1.DI, R1.Pin_0
  N3: NEOPIXEL1.GND, TRINKET1.no_name_yet#2, C1.-, S1.4
  N4: TRINKET1.no_name_yet#6, R2.Pin_1
  N5: TRINKET1.no_name_yet#7, R2.Pin_0, S1.2
  N6: TRINKET1.no_name_yet#9, R1.Pin_1

custom parts:
  Neopixel Strip -- Black (60/m): Neopixel Strip, Black, 60 pixels per meter.
  Trinket 5V: Adafruit Trinket 5V
